// Logisim project onr-training.circ as structural Verilog: 5 circuits, main circuit main
module main (
);

  wire j_k_ff_1_q, j_k_ff_1_qn, j_k_ff_2_q, j_k_ff_2_qn, j_k_ff_3_q, j_k_ff_3_qn, j_k_ff_4_q, j_k_ff_4_qn,
       j_k_ff_5_q, j_k_ff_5_qn, j_k_ff_6_q, j_k_ff_6_qn, j_k_ff_7_q, j_k_ff_7_qn, not_1_out, or_1_out,
       or_2_out, or_3_out, or_4_out, undriven, undriven_2, undriven_3, undriven_4, undriven_5, undriven_6,
       undriven_7, undriven_8, undriven_9, undriven_10, undriven_11, undriven_12, undriven_13;

  not not_1 (not_1_out, undriven);
  J_K_Flip_Flop j_k_ff_1 (
    .J(undriven), .clk(undriven_4), .K(not_1_out), .Q(j_k_ff_1_q), .Qn(j_k_ff_1_qn));  // open: preset, en, reset
  or or_1 (or_1_out, j_k_ff_1_q, undriven_2);
  J_K_Flip_Flop j_k_ff_2 (
    .J(j_k_ff_1_q), .clk(undriven_4), .K(j_k_ff_1_qn), .Q(j_k_ff_2_q), .Qn(j_k_ff_2_qn));  // open: preset, en, reset
  or or_2 (or_2_out, j_k_ff_2_q, undriven_3);
  J_K_Flip_Flop j_k_ff_3 (
    .J(j_k_ff_2_q), .clk(undriven_4), .K(j_k_ff_2_qn), .Q(j_k_ff_3_q), .Qn(j_k_ff_3_qn));  // open: preset, en, reset
  J_K_Flip_Flop j_k_ff_4 (
    .J(undriven_6), .clk(undriven_5), .K(undriven_7), .Q(j_k_ff_4_q), .Qn(j_k_ff_4_qn));  // open: preset, en, reset
  or or_3 (or_3_out, undriven_6, undriven_8);
  J_K_Flip_Flop j_k_ff_5 (
    .J(j_k_ff_4_q), .clk(undriven_5), .K(j_k_ff_4_qn), .Q(j_k_ff_5_q), .Qn(j_k_ff_5_qn));  // open: preset, en, reset
  J_K_Flip_Flop j_k_ff_6 (
    .J(undriven_10), .clk(undriven_9), .K(undriven_11), .Q(j_k_ff_6_q), .Qn(j_k_ff_6_qn));  // open: preset, en, reset
  or or_4 (or_4_out, undriven_12, undriven_13);
  J_K_Flip_Flop j_k_ff_7 (
    .J(j_k_ff_6_q), .clk(undriven_9), .K(j_k_ff_6_qn), .Q(j_k_ff_7_q), .Qn(j_k_ff_7_qn));  // open: preset, en, reset

  // Notes on the sheet:
  //   Module 1
  //   Module 2
  //   Module 3
endmodule

module Module_1 (
  input  CLK,
  input  Input,
  input  OR_1,
  input  OR_2,
  output Output_1,
  output Output_2,
  output Output_3,
  output Output_4,
  output Output_6,
  output Output_7
);

  wire j_k_ff_1_qn, j_k_ff_2_qn, not_1_out;

  not not_1 (not_1_out, Input);
  J_K_Flip_Flop j_k_ff_1 (
    .J(Input), .clk(CLK), .K(not_1_out), .Q(Output_3), .Qn(j_k_ff_1_qn));  // open: preset, en, reset
  or u_or_1 (Output_7, Output_3, OR_1);
  J_K_Flip_Flop j_k_ff_2 (
    .J(Output_3), .clk(CLK), .K(j_k_ff_1_qn), .Q(Output_4), .Qn(j_k_ff_2_qn));  // open: preset, en, reset
  or u_or_2 (Output_6, Output_4, OR_2);
  J_K_Flip_Flop j_k_ff_3 (
    .J(Output_4), .clk(CLK), .K(j_k_ff_2_qn), .Q(Output_1), .Qn(Output_2));  // open: preset, en, reset

  // Notes on the sheet:
  //   Module 1
endmodule

module Module_2 (
  input  CLK,
  input  Input_J,
  input  Input_K,
  input  Comb_1,
  output Ouput_Q,
  output Ouptut_Q,
  output Output_Reg,
  output Output_LED
);

  wire j_k_ff_1_qn;

  J_K_Flip_Flop j_k_ff_1 (
    .J(Input_J), .clk(CLK), .K(Input_K), .Q(Output_Reg), .Qn(j_k_ff_1_qn));  // open: preset, en, reset
  or or_1 (Output_LED, Input_J, Comb_1);
  J_K_Flip_Flop j_k_ff_2 (
    .J(Output_Reg), .clk(CLK), .K(j_k_ff_1_qn), .Q(Ouput_Q), .Qn(Ouptut_Q));  // open: preset, en, reset

  // Notes on the sheet:
  //   Module 2
endmodule

module Module_3 (
  input  CLK,
  input  Input_J,
  input  Input_K,
  input  Comb_1,
  input  Comb_2,
  output Output_Q,
  output Output_Q_2,
  output Output_Reg,
  output Output_OR
);

  wire j_k_ff_1_qn;

  J_K_Flip_Flop j_k_ff_1 (
    .J(Input_J), .clk(CLK), .K(Input_K), .Q(Output_Reg), .Qn(j_k_ff_1_qn));  // open: preset, en, reset
  or or_1 (Output_OR, Comb_1, Comb_2);
  J_K_Flip_Flop j_k_ff_2 (
    .J(Output_Reg), .clk(CLK), .K(j_k_ff_1_qn), .Q(Output_Q), .Qn(Output_Q_2));  // open: preset, en, reset

  // Notes on the sheet:
  //   Module 3
endmodule

module Example (
);

  wire button_1_out, clock_1_out, j_k_ff_1_qn, j_k_ff_2_qn, j_k_ff_3_qn, j_k_ff_4_qn, j_k_ff_5_qn,
       j_k_ff_6_qn, j_k_ff_7_qn, not_1_out, or_1_out, or_2_out, or_3_out, or_4_out, or_5_out, undriven;
  wire [3:0] j_k_ff_1_q, j_k_ff_5_q;

  Clock clock_1 (.out(clock_1_out));
  or or_1 (or_1_out, button_1_out, j_k_ff_5_q[3]);
  Button button_1 (.out(button_1_out));
  not not_1 (not_1_out, or_1_out);
  // NOT_Gate not_2 has open pins: in=open, out=not_1_out
  J_K_Flip_Flop j_k_ff_1 (
    .J(or_1_out), .clk(clock_1_out), .K(not_1_out), .Q(j_k_ff_1_q[0]), .Qn(j_k_ff_1_qn), .reset(undriven));  // open: preset, en
  J_K_Flip_Flop j_k_ff_2 (
    .J(j_k_ff_1_q[0]), .clk(clock_1_out), .K(j_k_ff_1_qn), .Q(j_k_ff_1_q[1]), .Qn(j_k_ff_2_qn),
    .reset(undriven));  // open: preset, en
  J_K_Flip_Flop j_k_ff_3 (
    .J(j_k_ff_1_q[1]), .clk(clock_1_out), .K(j_k_ff_2_qn), .Q(j_k_ff_1_q[2]), .Qn(j_k_ff_3_qn),
    .reset(undriven));  // open: preset, en
  J_K_Flip_Flop j_k_ff_4 (
    .J(j_k_ff_1_q[2]), .clk(clock_1_out), .K(j_k_ff_3_qn), .Q(j_k_ff_1_q[3]), .Qn(j_k_ff_4_qn),
    .reset(undriven));  // open: preset, en
  J_K_Flip_Flop j_k_ff_5 (
    .J(j_k_ff_1_q[3]), .clk(clock_1_out), .K(j_k_ff_4_qn), .Q(j_k_ff_5_q[0]), .Qn(j_k_ff_5_qn),
    .reset(undriven));  // open: preset, en
  J_K_Flip_Flop j_k_ff_6 (
    .J(j_k_ff_5_q[0]), .clk(clock_1_out), .K(j_k_ff_5_qn), .Q(j_k_ff_5_q[1]), .Qn(j_k_ff_6_qn),
    .reset(undriven));  // open: preset, en
  or or_2 (or_2_out, j_k_ff_1_q[0], j_k_ff_5_q[3]);
  or or_3 (or_3_out, j_k_ff_1_q[1], j_k_ff_5_q[2]);
  LED led_1 (.in(or_3_out));
  LED led_2 (.in(or_5_out));
  LED led_3 (.in(or_2_out));
  J_K_Flip_Flop j_k_ff_7 (
    .J(j_k_ff_5_q[1]), .clk(clock_1_out), .K(j_k_ff_6_qn), .Q(j_k_ff_5_q[2]), .Qn(j_k_ff_7_qn),
    .reset(undriven));  // open: preset, en
  or or_4 (or_4_out, j_k_ff_1_q[3], j_k_ff_5_q[0]);
  or or_5 (or_5_out, j_k_ff_1_q[2], j_k_ff_5_q[1]);
  LED led_4 (.in(or_4_out));
  J_K_Flip_Flop j_k_ff_8 (
    .J(j_k_ff_5_q[2]), .clk(clock_1_out), .K(j_k_ff_7_qn), .Q(j_k_ff_5_q[3]), .reset(undriven));  // open: Qn, preset, en

  // Notes on the sheet:
  //   CLK
  //   IN
endmodule
